# Fritzing sketch Akilli_oda_v1_frit (saved by Fritzing 0.8.7b)
breadboards: 1

parts:
  Eleman1 = Arduino Uno (Rev3)
  Relay_5V1 = Keyes Relay [package=THT]
  Eleman2 = Bluetooth HC-06
  R1 = Resistor [tolerance=±10% resistance=1k package=THT]
  R2 = Resistor [tolerance=±10% resistance=1k package=THT]
  R3 = Resistor [tolerance=±10% resistance=1k package=THT]
  J1 = Basic Servo
  Q1 = Basic FET N-Channel [package="TO220 [THT]"]
  Q2 = Basic FET N-Channel [package="TO220 [THT]"]
  Q3 = Basic FET N-Channel [package="TO220 [THT]"]
  R4 = Resistor [tolerance=±10% resistance=10k package=THT]
  R5 = Resistor [tolerance=±10% resistance=10k package=THT]
  R6 = Resistor [tolerance=±10% resistance=10k package=THT]
  RGB_Strip_LED2 = RGB Strip LED
  JACK2 = 2.1mm Barrel Jack with Terminal Block [part_number="12 V"]
  U1 = POT [package=pot_mammoth]
  S1 = Square Pushbutton
  R7 = Resistor [tolerance=±10% resistance=220 package=THT]

nets:
  N1: Eleman1.A0, U1.A
  N2: Eleman1.D8, R1.Pin_0
  N3: Eleman1.D11_PWM/MOSI, J1.pulse
  N4: Eleman1.D12/MISO, Relay_5V1.signal
  N5: Eleman1.D2, S1.leg1, R7.Pin_1
  N6: Eleman1.D3_PWM, Q3.gate, R5.Pin_1
  N7: Eleman1.D5_PWM, Q2.gate, R4.Pin_1
  N8: Eleman1.D6_PWM, Q1.gate, R6.Pin_1
  N9: Eleman1.D7, Eleman2.TXD
  VCC: Eleman1.5V, Relay_5V1.power, Eleman2.VCC, J1.vcc, U1.S, S1.leg0
  GND: Eleman1.GND, Relay_5V1.ground, Eleman2.GND, R3.Pin_1, J1.gnd, Q1.source, Q2.source, Q3.source, R4.Pin_0, R5.Pin_0, R6.Pin_0, JACK2.NEG, U1.E, R7.Pin_0
  N10: Eleman2.RXD, R1.Pin_1, R2.Pin_0
  N11: R2.Pin_1, R3.Pin_0
  N12: Q1.drain, RGB_Strip_LED2.Green_Connect
  N13: Q2.drain, RGB_Strip_LED2.Red_Connect
  N14: Q3.drain, RGB_Strip_LED2.Blue_Connect
  N15: RGB_Strip_LED2.Common_Connect, JACK2.POS

custom parts:
  Keyes Relay: The Keyes 5V relay module is suitable for SCM development, home appliance control. It uses a 5V~12V TIL control signal which can control DC / AC signal.
  RGB Strip LED: A tri-color Strip LED with red, green and blue. Based on LED SMD 5050 RGB Pin order: common cathode - green - red - blue
